# Fritzing sketch UnitaAttuatori (saved by Fritzing 0.9.3b)
breadboards: 1

parts:
  U1 = NodeMCU V3.0
  2_Channel_Relay1 = 2 Channel Power Relay
  KY-1 = Keyes Relay [package=THT]

nets:
  N1: U1.D0, KY-1.signal
  N2: U1.D1, 2_Channel_Relay1.IN1
  N3: U1.D2, 2_Channel_Relay1.IN2
  N4: U1.VU, 2_Channel_Relay1.VCC#14, KY-1.power
  GND: U1.GND, 2_Channel_Relay1.GND, KY-1.ground
  N5: 2_Channel_Relay1.JD-VCC, 2_Channel_Relay1.VCC#9

custom parts:
  NodeMCU V3.0: ESP8266 based NodeMCU
  2 Channel Power Relay: A 2 channel power relay. The module operates at 5V.
  Keyes Relay: The Keyes 5V relay module is suitable for SCM development, home appliance control. It uses a 5V~12V TIL control signal which can control DC / AC signal.
