# Fritzing sketch UnitaDiControllo (saved by Fritzing 0.9.3b)
breadboards: 1

parts:
  U1 = NodeMCU V3.0
  LCM1602_IIC1 = LCM1602 IIC [part_number="LCM1602 IIC" chip_label="LCM1602 IIC" package="DIP (Dual Inline) [THT]"]
  LCD1 = LCD screen
  S1 = Momentary Switch [package=ksa_sealed_tac_switch]
  S2 = Momentary Switch [package=ksa_sealed_tac_switch]
  S3 = Momentary Switch [package=ksa_sealed_tac_switch]
  R1 = Resistor [tolerance=±5% resistance=10k package="0603 [SMD]"]
  R2 = Resistor [tolerance=±5% resistance=10k package="0603 [SMD]"]
  R3 = Resistor [tolerance=±5% resistance=10k package="0603 [SMD]"]
  Blue_Led = LED - 3mm [color="Blue (525nm)" package="3 mm [THT]"]  # not connected
  Yellow_Led = LED - 3mm [color="Yellow (595nm)" package="3 mm [THT]"]
  Green_Led = LED - 3mm [color="Green (570nm)" package="3 mm [THT]"]
  R4 = Resistor [tolerance=±5% resistance=1k package="0402 [SMD]"]
  Red_Led = LED - 3mm [color="Red (633nm)" package="3 mm [THT]"]
  R5 = Resistor [tolerance=±5% resistance=220 package="0402 [SMD]"]
  R6 = Resistor [tolerance=±5% resistance=10k package="0603 [SMD]"]
  R7 = Resistor [tolerance=±5% resistance=100 package="0402 [SMD]"]

nets:
  N1: U1.D0, S2.3, S2.4, R1.Pin_1
  N2: U1.D1, LCM1602_IIC1.SCL
  N3: U1.D2, LCM1602_IIC1.SDA
  N4: U1.D4, R5.Pin_0
  N5: U1.D5, R7.Pin_0
  N6: U1.D6, R6.Pin_1
  N7: U1.D7, R4.Pin_1
  N8: U1.D8, S1.3, S1.4, R3.Pin_1
  N9: U1.VU, LCM1602_IIC1.VCC, S1.1, S1.2, S2.1, S2.2, S3.1, S3.2
  GND: U1.GND, LCM1602_IIC1.GND, R1.Pin_0, R2.Pin_0, R3.Pin_0, Yellow_Led.cathode, Green_Led.cathode, Red_Led.cathode
  N10: U1.A0, S3.3, S3.4, R2.Pin_1
  VSS: LCM1602_IIC1.VSS, LCD1.VSS
  VDD: LCM1602_IIC1.VDD, LCD1.VDD
  N11: LCM1602_IIC1.V0, LCD1.V0
  N12: LCM1602_IIC1.RS, LCD1.RS
  N13: LCM1602_IIC1.RW, LCD1.R/W
  N14: LCM1602_IIC1.E, LCD1.E
  N15: LCM1602_IIC1.D0, LCD1.DB0
  N16: LCM1602_IIC1.D1, LCD1.DB1
  N17: LCM1602_IIC1.D2, LCD1.DB2
  N18: LCM1602_IIC1.D3, LCD1.DB3
  N19: LCM1602_IIC1.D4, LCD1.DB4
  N20: LCM1602_IIC1.D5, LCD1.DB5
  N21: LCM1602_IIC1.D6, LCD1.DB6
  N22: LCM1602_IIC1.D7, LCD1.DB7
  N23: LCM1602_IIC1.A, LCD1.LED-
  N24: LCM1602_IIC1.K, LCD1.LED+
  N25: LCM1602_IIC1.LED_A, LCM1602_IIC1.LED_B
  N26: Yellow_Led.anode, R7.Pin_1
  N27: Green_Led.anode, R5.Pin_1
  N28: R4.Pin_0, Red_Led.anode

custom parts:
  NodeMCU V3.0: ESP8266 based NodeMCU
  LCM1602 IIC: I2C-Module to use a 1602 or 2004 LCD on with the wire.h libory Serial LCD Modul
  LCD screen: A standard character display, usually with 2x16 characters. Comes in many colors.
