# Fritzing sketch UnitaSensori (saved by Fritzing 0.9.3b)
breadboards: 1

parts:
  U1 = NodeMCU V3.0
  DS1 = DS18B20 1-Wire Temperature Sensor Probe Cable
  R1 = Resistor [tolerance=±5% resistance=4.7k package="0402 [SMD]"]
  Part3 = KY-018 Photoresistor Module [package="Breakout board"]
  YL-83_-_Control_Board1 = YL-83 Rain Sensor - Control Board
  YL-83_-_Detection_Board1 = YL-83 Rain Sensor - Detection Board
  Componente1 = FC-28 Soil Hygrometer Module - Probe
  YL-83_-_Control_Board2 = YL-83 Rain Sensor - Control Board
  Part4 = KY-015 Temperature & Humidity Sensor Module [package="Breakout board"]
  U2 = SWITCH-SPST-2 [package=switch-spst-vertical]
  R2 = Resistor [tolerance=±5% resistance=10k package="0603 [SMD]"]

nets:
  N1: U1.D0, Part4.S
  N2: U1.D1, DS1.shield, R1.Pin_1
  N3: U1.D2, YL-83_-_Control_Board1.DO
  N4: U1.D3, YL-83_-_Control_Board2.DO
  N5: U1.D4, U2.P, R2.Pin_0
  VCC: U1.3V3, YL-83_-_Control_Board1.VCC, YL-83_-_Control_Board2.VCC
  GND: U1.GND#13, U1.GND#33, YL-83_-_Control_Board1.GND, YL-83_-_Control_Board2.GND
  VIN: U1.VU, DS1.VDD, R1.Pin_0, Part3.Vin, Part4.Vin, U2.O
  N6: U1.GND#41, DS1.GND, Part3.-, Part4.-, R2.Pin_1
  N7: YL-83_-_Control_Board1.POS, YL-83_-_Detection_Board1.POS
  N8: YL-83_-_Control_Board1.NEG, YL-83_-_Detection_Board1.NEG
  N9: Componente1.POS, YL-83_-_Control_Board2.POS
  N10: Componente1.NEG, YL-83_-_Control_Board2.NEG

custom parts:
  NodeMCU V3.0: ESP8266 based NodeMCU
  KY-018 Photoresistor Module: KY-018 Photoresistor module, used to measure light intensity. It can determine the presence or absence of light.
  YL-83 Rain Sensor - Control Board: The YL-83 is a rain sensor that has more resistance when dry and less resistance when wet. The module runs at 5V.
  YL-83 Rain Sensor - Detection Board: The YL-83 is a rain sensor that has more resistance when dry and less resistance when wet. The module runs at 5V.
  FC-28 Soil Hygrometer Module - Probe: The FC-28 is a soil hygrometer module that uses the Texas Instruments LM393 comparator chip to provide an analog measurement of soil humidity.
  KY-015 Temperature & Humidity Sensor Module: KY-015 temperature and humidity sensor module, provides a low-latency serial interface to measure humidity and temperature.
